# Fritzing sketch Montage_OLED_DTH22_RTC_PIR (saved by Fritzing 0.9.3b)
breadboards: 1

parts:
  Composant1 = Arduino Leonardo (Rev3b)
  Squix1 = OLED 0.96" 128x64 I2C SSD1306
  DHT1 = DHT22 Humidity and Temperature Sensor
  Tiny_RTC1 = Tiny RTC
  PIR1 = PIR sensor
  R1 = Resistor [tolerance=±5% resistance=4.7k package=THT]

nets:
  N1: Composant1.D4/A6, DHT1.DATA, R1.Pin_0
  N2: Composant1.D7, PIR1.SIG
  GND: Composant1.GND, Squix1.GND, DHT1.GND, Tiny_RTC1.GND, PIR1.GND
  VCC: Composant1.VIN, Squix1.VCC, DHT1.VDD, Tiny_RTC1.VCC, PIR1.VDD, R1.Pin_1
  N3: Composant1.SDA, Squix1.SCA, Tiny_RTC1.SDA
  N4: Composant1.SCL, Squix1.SCL, Tiny_RTC1.SCL

notes:
  Cemontage permet d'afficher la température,l'humidité, la date et l'heure sur un écran OLED. Le capteur de mouvement permet d'allumer l'écran durant un temps X(réglage du tiny RTC).
  résistance du DHT22 : 4.7kΩ
  ecran + tiny RTC couplés : protocole i2c

custom parts:
  Tiny RTC: Tiny RTC I2C module DS1370Z RTC and AT24C32 EEPROM
